// Logisim project MultiplicadorRTL.circ as structural Verilog: 2 circuits, main circuit main
module main (
  input  [3:0] A,
  input  [3:0] B,
  input  Start
);

  wire A_out, Add, adder_1_cout, Clock, Co, controladoras_1_add2, controladoras_1_done2,
       controladoras_1_wait2, Done, Last, Load, not_1_out, Shift, WAIT_q;
  wire [2:1] counter_1_q;
  wire [3:0] _4_bit_out, bit_extender_1_out, M3;
  wire [7:0] M;

  Clock u_Clock (.out(Clock));
  D_Flip_Flop WAIT (.clk(Clock), .D(controladoras_1_wait2), .Q(WAIT_q));  // open: Qn, preset, en, reset
  D_Flip_Flop u_ADD (.clk(Clock), .D(controladoras_1_add2), .Q(Add));  // open: Qn, preset, en, reset
  D_Flip_Flop u_DONE (.clk(Clock), .D(controladoras_1_done2), .Q(Done));  // open: Qn, preset, en, reset
  // Probe on A
  Controladoras controladoras_1 (
    .done(Done), .add(Add), .done2(controladoras_1_done2), .\wait (WAIT_q), .start(Start),
    .add2(controladoras_1_add2), .last(Last), .wait2(controladoras_1_wait2), .load(Load));
  LED led_1 (.in(Done));
  // Probe on B
  // Probe on M
  Counter #(.width(3), .max('h7)) counter_1 (
    .count(Add), .Q({counter_1_q, Shift}), .carry(Last), .clk(Clock), .clr(Load));  // open: load, D
  Shift_Register #(.length(4)) u_A (
    .shift(Shift), .in(1'b0), .clk(Clock), .out(A_out), .load(Load), .d0(A[3]), .d1(A[2]), .d2(A[1]),
    .d3(A[0]));  // open: clr, q0, q1, q2, q3
  assign bit_extender_1_out = {{3{A_out}}, A_out};  // Bit_Extender bit_extender_1
  not not_1 (not_1_out, Shift);
  Shift_Register u_M (
    .shift(Shift), .in(Co), .clk(Clock), .load(not_1_out), .clr(Load), .d0(M3[3]), .q0(M[7]), .d1(M3[2]),
    .q1(M[6]), .d2(M3[1]), .q2(M[5]), .d3(M3[0]), .q3(M[4]), .d4(M[3]), .q4(M[3]), .d5(M[2]), .q5(M[2]),
    .d6(M[1]), .q6(M[1]), .d7(M[0]), .q7(M[0]));  // open: out
  assign _4_bit_out = B & bit_extender_1_out;  // AND_Gate _4_bit, 4 bits wide
  Adder #(.width(4)) adder_1 (.a(_4_bit_out), .b(M[7:4]), .out(M3), .cin(1'b0), .cout(adder_1_cout));
  D_Flip_Flop d_ff_1 (.clk(Clock), .D(adder_1_cout), .Q(Co), .reset(Load));  // open: Qn, preset, en

  // Other names for the same wires on the sheet: M1[3:0] = M[3:0]; M2[3:0] = M[7:4]

  // Notes on the sheet:
  //   sWait
  //   sAdd
  //   sDone
  //   Entradas
  //   nWait
  //   nAdd
  //   nDone
  //   Resultados
  //   =
  //   *
  //   CAMINHO DE DADOS
  //   Até 8
endmodule

module Controladoras (
  input  done,
  input  add,
  input  \wait ,
  input  start,
  input  last,
  output done2,
  output add2,
  output wait2,
  output load
);

  wire and_1_out, and_2_out, and_3_out, and_4_out, and_5_out, and_6_out, and_7_out, and_8_out, not_1_out,
       not_2_out, not_3_out, not_4_out, not_5_out, not_6_out, not_7_out, not_8_out, not_9_out, not_10_out,
       not_11_out;

  not not_1 (not_1_out, add);
  not not_2 (not_2_out, last);
  not not_3 (not_3_out, last);
  not not_4 (not_4_out, done);
  not not_5 (not_5_out, add);
  not not_6 (not_6_out, \wait );
  not not_7 (not_7_out, add);
  not not_8 (not_8_out, start);
  not not_9 (not_9_out, start);
  not not_10 (not_10_out, done);
  not not_11 (not_11_out, add);
  and and_1 (and_1_out, add, last);
  and and_2 (and_2_out, done, start);
  and and_3 (and_3_out, done, not_1_out, \wait , not_2_out);
  and and_4 (and_4_out, \wait , start);
  and and_5 (and_5_out, add, not_3_out);
  and and_6 (and_6_out, not_4_out, not_5_out, not_6_out);
  and and_7 (and_7_out, not_7_out, not_8_out);
  and and_8 (and_8_out, done, not_9_out);
  and and_9 (load, not_10_out, not_11_out, \wait , start);
  or or_1 (done2, and_1_out, and_2_out, and_3_out);
  or or_2 (add2, and_4_out, and_5_out);
  or or_3 (wait2, and_6_out, and_7_out, and_8_out);
endmodule
